// Logisim project immGenCirc.circ as structural Verilog: 10 circuits, main circuit AND2
module AND2 (
  input  A,
  input  B,
  output RESULT
);

  and and_1 (RESULT, A, B);

  // Notes on the sheet:
  //   Sample Circuit
endmodule

module NAND2 (
  input  A,
  input  B,
  output RESULT
);

  wire and_1_out;

  and and_1 (and_1_out, A, B);
  not not_1 (RESULT, and_1_out);
endmodule

module NOR2 (
  input  A,
  input  B,
  output RESULT
);

  wire or_1_out;

  or or_1 (or_1_out, A, B);
  not not_1 (RESULT, or_1_out);
endmodule

module XOR2 (
  input  A,
  input  B,
  output RESULT
);

  wire and_1_out, and_2_out, not_1_out, not_2_out;

  not not_1 (not_1_out, B);
  not not_2 (not_2_out, A);
  and and_1 (and_1_out, A, not_1_out);
  and and_2 (and_2_out, not_2_out, B);
  or or_1 (RESULT, and_1_out, and_2_out);
endmodule

module MUX2 (
  input  A,
  input  B,
  input  SEL,
  output RESULT
);

  wire and_1_out, and_2_out, not_1_out;

  not not_1 (not_1_out, SEL);
  and and_1 (and_1_out, A, SEL);
  and and_2 (and_2_out, B, not_1_out);
  or or_1 (RESULT, and_1_out, and_2_out);
endmodule

module MUX4 (
  input  A,
  input  B,
  input  C,
  input  D,
  input  SEL0,
  input  SEL1,
  output RESULT
);

  wire and_1_out, and_2_out, and_3_out, and_4_out, and_5_out, and_6_out, and_7_out, and_8_out, not_1_out,
       not_2_out, or_1_out, or_2_out;

  not not_1 (not_1_out, SEL0);
  not not_2 (not_2_out, SEL1);
  and and_1 (and_1_out, A, not_1_out);
  and and_2 (and_2_out, B, not_2_out);
  and and_3 (and_3_out, C, not_1_out);
  and and_4 (and_4_out, D, SEL1);
  and and_5 (and_5_out, and_1_out, not_2_out);
  and and_6 (and_6_out, and_2_out, SEL0);
  and and_7 (and_7_out, and_3_out, SEL1);
  and and_8 (and_8_out, and_4_out, SEL0);
  or or_1 (or_1_out, and_5_out, and_6_out);
  or or_2 (or_2_out, and_7_out, and_8_out);
  or or_3 (RESULT, or_1_out, or_2_out);
endmodule

module oneBitFullAdder (
  input  A,
  input  B,
  input  Cin,
  output S,
  output Cout
);

  wire and_1_out, and_2_out, xor2_1_result;

  XOR2 xor2_1 (.A(A), .B(B), .RESULT(xor2_1_result));
  and and_1 (and_1_out, xor2_1_result, Cin);
  and and_2 (and_2_out, A, B);
  XOR2 xor2_2 (.A(xor2_1_result), .B(Cin), .RESULT(S));
  or or_1 (Cout, and_1_out, and_2_out);
endmodule

module oneBitALU (
  input  [1:0] Operation,
  input  A,
  input  B,
  input  Binvert,
  input  CarryIn,
  output Result,
  output CarryOut
);

  wire and_1_out, onebitfulladder_1_s, or_1_out, xor2_1_result, xor2_2_result;

  XOR2 xor2_1 (.A(Binvert), .B(B), .RESULT(xor2_1_result));
  and and_1 (and_1_out, A, B);
  or or_1 (or_1_out, A, B);
  XOR2 xor2_2 (.A(A), .B(B), .RESULT(xor2_2_result));
  oneBitFullAdder onebitfulladder_1 (.A(A), .B(xor2_1_result), .Cin(CarryIn), .S(onebitfulladder_1_s), .Cout(CarryOut));
  MUX4 mux4_1 (
    .A(and_1_out), .B(or_1_out), .C(xor2_2_result), .D(onebitfulladder_1_s), .SEL0(Operation[0]),
    .SEL1(Operation[1]), .RESULT(Result));
endmodule

module fourBitALU (
  input  Binvert,
  input  CarryIn,
  input  [1:0] Operation,
  input  [3:0] A,
  input  [3:0] B,
  output [3:0] Result,
  output CarryOut
);

  wire ALU0_carryout, ALU1_carryout, ALU2_carryout;

  oneBitALU ALU0 (
    .Operation(Operation), .A(A[0]), .B(B[0]), .Binvert(Binvert), .CarryIn(CarryIn), .Result(Result[0]),
    .CarryOut(ALU0_carryout));
  oneBitALU ALU1 (
    .Operation(Operation), .A(A[1]), .B(B[1]), .Binvert(Binvert), .CarryIn(ALU0_carryout),
    .Result(Result[1]), .CarryOut(ALU1_carryout));
  oneBitALU ALU2 (
    .Operation(Operation), .A(A[2]), .B(B[2]), .Binvert(Binvert), .CarryIn(ALU1_carryout),
    .Result(Result[2]), .CarryOut(ALU2_carryout));
  oneBitALU ALU3 (
    .Operation(Operation), .A(A[3]), .B(B[3]), .Binvert(Binvert), .CarryIn(ALU2_carryout),
    .Result(Result[3]), .CarryOut(CarryOut));
endmodule

module ImmGenCircuit (
  input  [31:0] Instr,
  output [31:0] Imm32
);


  assign Imm32[10:5] = Instr[30:25];

  // Other names for the same wires on the sheet: I30_25[5:0] = Instr[30:25]; I5 = Instr[5]; I6_5[1:0] = Instr[6:5];
  //   I6 = Instr[6]
endmodule
