// Logisim project immGenCirc1.circ as structural Verilog
module ImmGenCircuit (
  input  [31:0] Instr,
  input  in_2,
  output [31:0] Imm32
);

  assign Imm32[31:12] = {{19{Instr[31]}}, Instr[31]};  // Bit_Extender bit_extender_1
  Multiplexer #(.select(2)) multiplexer_1 (
    .in0(Instr[20]), .in1(Instr[7]), .in2(in_2), .out(Imm32[0]), .sel(Instr[6:5]));  // open: in3
  Multiplexer #(.width(4)) multiplexer_2 (.in0(Instr[24:21]), .in1(Instr[11:8]), .out(Imm32[4:1]), .sel(Instr[5]));
  Multiplexer multiplexer_3 (.in0(Instr[31]), .in1(Instr[7]), .out(Imm32[11]), .sel(Instr[6]));

  assign Imm32[10:5] = Instr[30:25];

  // Other names for the same wires on the sheet: I0 = Imm32[0]; I4_1[3:0] = Imm32[4:1]; I30_25[5:0] = Instr[30:25];
  //   I11 = Imm32[11]; I31_12[19:0] = Imm32[31:12]; I5 = Instr[5]; I6_5[1:0] = Instr[6:5]; I6 = Instr[6];
  //   I7 = Instr[7]; I11_8[3:0] = Instr[11:8]; I20 = Instr[20]; I24_21[3:0] = Instr[24:21]; I31 = Instr[31]
endmodule
