// Logisim project lab4.circ as structural Verilog: 4 circuits, main circuit main
module main (
  input  in_1,
  input  in_2,
  output out_3
);

  and and_1 (out_3, in_1, in_2);
endmodule

module oneBitFullAdder (
  input  A,
  input  B,
  input  Cin,
  output S,
  output Cout
);

  wire and_1_out, and_2_out, xor2_1_p2;

  // XOR2 xor2_1: pin names not known; wires that end beside it: A, xor2_1_p2, xor2_1_p2, Cin
  and and_1 (and_1_out, xor2_1_p2, Cin);
  and and_2 (and_2_out, A, B);
  // XOR2 xor2_2: pin names not known; wires that end beside it: S
  or or_1 (Cout, and_1_out, and_2_out);
endmodule

module oneBitALU (
  input  [1:0] Operation,
  input  A,
  input  B,
  input  Binvert,
  input  CarryIn,
  output Result,
  output CarryOut
);

  wire and_1_out, or_1_out, xor_1_p3, xor_2_p3, xor_2_p7;

  // XOR_Gate xor_1: pin names not known; wires that end beside it: B, Binvert, xor_1_p3
  and and_1 (and_1_out, A, B);
  or or_1 (or_1_out, A, B);
  // XOR__Gate xor_2: pin names not known; wires that end beside it: A, B, xor_2_p3, and_1_out, or_1_out, xor_2_p3, xor_2_p7, Operation[0], Operation[1]
  oneBitFullAdder onebitfulladder_1 (.A(A), .B(xor_1_p3), .Cin(CarryIn), .S(xor_2_p7), .Cout(CarryOut));
  Multiplexer #(.width(4)) multiplexer_1 ();  // open: in0, in1, out, sel
endmodule

module fourBitALU (
  input  Binvert,
  input  CarryIn,
  input  [1:0] Operation,
  input  [3:0] A,
  input  [3:0] B,
  output [3:0] Result,
  output CarryOut
);

  wire ALU0_carryout, ALU1_carryout, ALU2_carryout;

  oneBitALU ALU0 (
    .Operation(Operation), .A(A[0]), .B(B[0]), .Binvert(Binvert), .CarryIn(CarryIn), .Result(Result[0]),
    .CarryOut(ALU0_carryout));
  oneBitALU ALU1 (
    .Operation(Operation), .A(A[1]), .B(B[1]), .Binvert(Binvert), .CarryIn(ALU0_carryout),
    .Result(Result[1]), .CarryOut(ALU1_carryout));
  oneBitALU ALU2 (
    .Operation(Operation), .A(A[2]), .B(B[2]), .Binvert(Binvert), .CarryIn(ALU1_carryout),
    .Result(Result[2]), .CarryOut(ALU2_carryout));
  oneBitALU ALU3 (
    .Operation(Operation), .A(A[3]), .B(B[3]), .Binvert(Binvert), .CarryIn(ALU2_carryout),
    .Result(Result[3]), .CarryOut(CarryOut));
endmodule
