// Logisim project lab5.circ as structural Verilog: 12 circuits, main circuit main_control_circuit
module oneBitFullAdder (
  input  A,
  input  B,
  input  Cin,
  output S,
  output Cout
);

  wire and_1_out, and_2_out, xor_1_out;

  xor xor_1 (xor_1_out, A, B);
  and and_1 (and_1_out, xor_1_out, Cin);
  and and_2 (and_2_out, A, B);
  xor xor_2 (S, xor_1_out, Cin);
  or or_1 (Cout, and_1_out, and_2_out);
endmodule

module oneBitALU (
  input  A,
  input  [3:0] ALU_Ctrl,
  input  B,
  input  CarryIn,
  output Result,
  output CarryOut
);

  wire and_1_out, multiplexer_1_out, onebitfulladder_1_s, or_1_out, shifter_1_out, shifter_2_out,
       shifter_3_out, xor_1_out, xor_2_out;

  xor xor_1 (xor_1_out, B, ALU_Ctrl[2]);
  and and_1 (and_1_out, A, B);
  or or_1 (or_1_out, A, B);
  xor xor_2 (xor_2_out, A, B);
  Multiplexer multiplexer_1 (.in0(CarryIn), .in1(ALU_Ctrl[2]), .out(multiplexer_1_out), .sel(ALU_Ctrl[2]));
  Shifter #(.width(1)) shifter_1 (.in(A), .\dist (B), .out(shifter_1_out));
  Shifter #(.shift("lr"), .width(1)) shifter_2 (.in(A), .\dist (B), .out(shifter_2_out));
  Shifter #(.shift("ar"), .width(1)) shifter_3 (.in(A), .\dist (B), .out(shifter_3_out));
  oneBitFullAdder onebitfulladder_1 (
    .A(A), .B(xor_1_out), .Cin(multiplexer_1_out), .S(onebitfulladder_1_s), .Cout(CarryOut));
  Multiplexer #(.select(4)) multiplexer_2 (
    .in0(and_1_out), .in1(or_1_out), .in2(xor_2_out), .in3(onebitfulladder_1_s), .in4(onebitfulladder_1_s),
    .in5(shifter_1_out), .in6(shifter_2_out), .in7(shifter_3_out), .out(Result), .sel(ALU_Ctrl));  // open: in8, in9, in10, in11, in12, in13, in14, in15

  // Other names for the same wires on the sheet: Binvert = ALU_Ctrl[2]
endmodule

module fourBitALU (
  input  CarryIn,
  input  [3:0] ALU_Ctrl,
  input  [3:0] A,
  input  [3:0] B,
  output [3:0] Result,
  output CarryOut
);

  wire ALU0_carryout, ALU1_carryout, ALU2_carryout;

  oneBitALU ALU0 (
    .A(A[0]), .ALU_Ctrl(ALU_Ctrl), .B(B[0]), .CarryIn(CarryIn), .Result(Result[0]), .CarryOut(ALU0_carryout));
  oneBitALU ALU1 (
    .A(A[1]), .ALU_Ctrl(ALU_Ctrl), .B(B[1]), .CarryIn(ALU0_carryout), .Result(Result[1]),
    .CarryOut(ALU1_carryout));
  oneBitALU ALU2 (
    .A(A[2]), .ALU_Ctrl(ALU_Ctrl), .B(B[2]), .CarryIn(ALU1_carryout), .Result(Result[2]),
    .CarryOut(ALU2_carryout));
  oneBitALU ALU3 (
    .A(A[3]), .ALU_Ctrl(ALU_Ctrl), .B(B[3]), .CarryIn(ALU2_carryout), .Result(Result[3]), .CarryOut(CarryOut));
endmodule

module thirtyTwoBitALU (
  input  CarryIn,
  input  [3:0] ALU_Ctrl,
  input  [31:0] A,
  input  [31:0] B,
  output [31:0] Result,
  output CarryOut
);

  wire fourbitalu_1_carryout, fourbitalu_2_carryout, fourbitalu_3_carryout, fourbitalu_4_carryout,
       fourbitalu_5_carryout, fourbitalu_6_carryout, fourbitalu_7_carryout;
  wire [3:0] fourbitalu_1_result, fourbitalu_2_result, fourbitalu_3_result, fourbitalu_4_result,
       fourbitalu_5_result, fourbitalu_6_result, fourbitalu_7_result, fourbitalu_8_result;
  wire [31:0] shifter_1_out, shifter_2_out, shifter_3_out;

  Shifter #(.width(32)) shifter_1 (.in(A), .out(shifter_1_out));  // open: dist
  Shifter #(.shift("lr"), .width(32)) shifter_2 (.in(A), .out(shifter_2_out));  // open: dist
  Shifter #(.shift("ar"), .width(32)) shifter_3 (.in(A), .out(shifter_3_out));  // open: dist
  fourBitALU fourbitalu_1 (
    .CarryIn(CarryIn), .ALU_Ctrl(ALU_Ctrl), .A(A[3:0]), .B(B[3:0]), .Result(fourbitalu_1_result),
    .CarryOut(fourbitalu_1_carryout));
  fourBitALU fourbitalu_2 (
    .CarryIn(fourbitalu_1_carryout), .ALU_Ctrl(ALU_Ctrl), .A(A[7:4]), .B(B[7:4]),
    .Result(fourbitalu_2_result), .CarryOut(fourbitalu_2_carryout));
  fourBitALU fourbitalu_3 (
    .CarryIn(fourbitalu_2_carryout), .ALU_Ctrl(ALU_Ctrl), .A(A[11:8]), .B(B[11:8]),
    .Result(fourbitalu_3_result), .CarryOut(fourbitalu_3_carryout));
  fourBitALU fourbitalu_4 (
    .CarryIn(fourbitalu_3_carryout), .ALU_Ctrl(ALU_Ctrl), .A(A[15:12]), .B(B[15:12]),
    .Result(fourbitalu_4_result), .CarryOut(fourbitalu_4_carryout));
  fourBitALU fourbitalu_5 (
    .CarryIn(fourbitalu_4_carryout), .ALU_Ctrl(ALU_Ctrl), .A(A[19:16]), .B(B[19:16]),
    .Result(fourbitalu_5_result), .CarryOut(fourbitalu_5_carryout));
  fourBitALU fourbitalu_6 (
    .CarryIn(fourbitalu_5_carryout), .ALU_Ctrl(ALU_Ctrl), .A(A[23:20]), .B(B[23:20]),
    .Result(fourbitalu_6_result), .CarryOut(fourbitalu_6_carryout));
  fourBitALU fourbitalu_7 (
    .CarryIn(fourbitalu_6_carryout), .ALU_Ctrl(ALU_Ctrl), .A(A[27:24]), .B(B[27:24]),
    .Result(fourbitalu_7_result), .CarryOut(fourbitalu_7_carryout));
  fourBitALU fourbitalu_8 (
    .CarryIn(fourbitalu_7_carryout), .ALU_Ctrl(ALU_Ctrl), .A(A[31:28]), .B(B[31:28]),
    .Result(fourbitalu_8_result), .CarryOut(CarryOut));
  Multiplexer #(.select(4), .width(32)) multiplexer_1 (
    .in0({fourbitalu_8_result, fourbitalu_7_result, fourbitalu_6_result, fourbitalu_5_result, fourbitalu_4_result, fourbitalu_3_result, fourbitalu_2_result, fourbitalu_1_result}),
    .in1({fourbitalu_8_result, fourbitalu_7_result, fourbitalu_6_result, fourbitalu_5_result, fourbitalu_4_result, fourbitalu_3_result, fourbitalu_2_result, fourbitalu_1_result}),
    .in2({fourbitalu_8_result, fourbitalu_7_result, fourbitalu_6_result, fourbitalu_5_result, fourbitalu_4_result, fourbitalu_3_result, fourbitalu_2_result, fourbitalu_1_result}),
    .in3({fourbitalu_8_result, fourbitalu_7_result, fourbitalu_6_result, fourbitalu_5_result, fourbitalu_4_result, fourbitalu_3_result, fourbitalu_2_result, fourbitalu_1_result}),
    .in4({fourbitalu_8_result, fourbitalu_7_result, fourbitalu_6_result, fourbitalu_5_result, fourbitalu_4_result, fourbitalu_3_result, fourbitalu_2_result, fourbitalu_1_result}),
    .in5(shifter_1_out), .in6(shifter_2_out), .in7(shifter_3_out), .out(Result), .sel(ALU_Ctrl));  // open: in8, in9, in10, in11, in12, in13, in14, in15
endmodule

module ALU_Ctrl_Circuit (
  input  I30,
  input  I14,
  input  I13,
  input  I12,
  input  I5,
  input  I4,
  output ALU_Ctrl3,
  output ALU_Ctrl2,
  output ALU_Ctrl1,
  output ALU_Ctrl0,
  output ALU_Src
);

  wire and_1_out, and_2_out, and_3_out, and_4_out, and_5_out, and_6_out, and_7_out, and_8_out, and_9_out,
       and_10_out, and_11_out, and_12_out, and_13_out, not_1_out, not_2_out, not_3_out, not_4_out, not_5_out,
       not_6_out;

  not not_1 (not_1_out, I30);
  not not_2 (not_2_out, I14);
  not not_3 (not_3_out, I13);
  not not_4 (not_4_out, I12);
  not not_5 (not_5_out, I5);
  not not_6 (not_6_out, I4);
  and and_1 (and_1_out, I30, not_3_out, I5);
  and and_2 (and_2_out, not_1_out, not_3_out, I12, I4);
  or or_1 (ALU_Ctrl2, and_1_out, and_2_out, and_3_out);
  and and_3 (and_3_out, I14, not_3_out, I12, I4);
  and and_4 (and_4_out, not_1_out, not_3_out, not_4_out);
  and and_5 (and_5_out, I14, not_3_out);
  and and_6 (and_6_out, I30, not_3_out, I12);
  and and_7 (and_7_out, not_3_out, not_4_out, not_5_out);
  and and_8 (and_8_out, not_1_out, not_2_out);
  and and_9 (and_9_out, I13, not_4_out);
  and and_10 (and_10_out, not_2_out, not_5_out);
  and and_11 (and_11_out, not_2_out, not_6_out);
  and and_12 (and_12_out, I30, not_3_out, I12, I4);
  and and_13 (and_13_out, not_2_out, I12);
  or or_2 (ALU_Src, not_5_out, not_6_out);
  or or_3 (ALU_Ctrl1, and_4_out, not_6_out, and_5_out, and_6_out, and_7_out);
  or or_4 (ALU_Ctrl0, and_8_out, and_9_out, and_10_out, and_11_out, and_12_out, and_13_out);

  assign ALU_Ctrl3 = 1'b0;
endmodule

module Register32Bit (
  input  [4:0] RReg1,
  input  [4:0] RReg2,
  input  [4:0] WReg,
  input  [31:0] WData,
  input  Write,
  input  Clock_in,
  output [31:0] RData1,
  output [31:0] RData2
);

  wire and_1_out, and_2_out, and_3_out, and_4_out, and_5_out, and_6_out, and_7_out, and_8_out, and_9_out,
       and_10_out, and_11_out, and_12_out, and_13_out, and_14_out, and_15_out, and_16_out, and_17_out,
       and_18_out, and_19_out, and_20_out, and_21_out, and_22_out, and_23_out, and_24_out, and_25_out,
       and_26_out, and_27_out, and_28_out, and_29_out, and_30_out, and_31_out, and_32_out, decoder_1_out0,
       decoder_1_out1, decoder_1_out2, decoder_1_out3, decoder_1_out4, decoder_1_out5, decoder_1_out6,
       decoder_1_out7, decoder_1_out8, decoder_1_out9, decoder_1_out10, decoder_1_out11, decoder_1_out12,
       decoder_1_out13, decoder_1_out14, decoder_1_out15, decoder_1_out16, decoder_1_out17, decoder_1_out18,
       decoder_1_out19, decoder_1_out20, decoder_1_out21, decoder_1_out22, decoder_1_out23, decoder_1_out24,
       decoder_1_out25, decoder_1_out26, decoder_1_out27, decoder_1_out28, decoder_1_out29, decoder_1_out30,
       decoder_1_out31;
  wire [31:0] register_1_q, register_2_q, register_3_q, register_4_q, register_5_q, register_6_q,
       register_7_q, register_8_q, register_9_q, register_10_q, register_11_q, register_12_q, x0_q, x1_q,
       x2_q, x3_q, x4_q, x5_q, x6_q, x7_q, x8_q, x9_q, x10_q, x11_q, x12_q, x13_q, x14_q, x15_q, x16_q,
       x21_q, x26_q, x31_q;

  Decoder #(.select(5)) decoder_1 (
    .out0(decoder_1_out0), .out1(decoder_1_out1), .out2(decoder_1_out2), .out3(decoder_1_out3),
    .out4(decoder_1_out4), .out5(decoder_1_out5), .out6(decoder_1_out6), .out7(decoder_1_out7),
    .out8(decoder_1_out8), .out9(decoder_1_out9), .out10(decoder_1_out10), .out11(decoder_1_out11),
    .out12(decoder_1_out12), .out13(decoder_1_out13), .out14(decoder_1_out14), .out15(decoder_1_out15),
    .out16(decoder_1_out16), .out17(decoder_1_out17), .out18(decoder_1_out18), .out19(decoder_1_out19),
    .out20(decoder_1_out20), .out21(decoder_1_out21), .out22(decoder_1_out22), .out23(decoder_1_out23),
    .out24(decoder_1_out24), .out25(decoder_1_out25), .out26(decoder_1_out26), .out27(decoder_1_out27),
    .out28(decoder_1_out28), .out29(decoder_1_out29), .out30(decoder_1_out30), .out31(decoder_1_out31),
    .sel(WReg));  // open: en
  Multiplexer #(.select(5), .width(32)) multiplexer_1 (
    .in0(x0_q), .in1(x1_q), .in2(x2_q), .in3(x3_q), .in4(x4_q), .in5(x5_q), .in6(x6_q), .in7(x7_q),
    .in8(x8_q), .in9(x9_q), .in10(x10_q), .in11(x11_q), .in12(x12_q), .in13(x13_q), .in14(x14_q),
    .in15(x15_q), .in16(x16_q), .in17(register_1_q), .in18(register_2_q), .in19(register_3_q),
    .in20(register_4_q), .in21(x21_q), .in22(register_5_q), .in23(register_6_q), .in24(register_7_q),
    .in25(register_8_q), .in26(x26_q), .in27(register_9_q), .in28(register_10_q), .in29(register_11_q),
    .in30(register_12_q), .in31(x31_q), .out(RData1), .sel(RReg1));
  Register #(.width(32)) x0 (.D(WData), .en(and_1_out), .clk(Clock_in), .Q(x0_q));  // open: clr
  and and_1 (and_1_out, decoder_1_out0, Write);
  Register #(.width(32)) x1 (.D(WData), .en(and_2_out), .clk(Clock_in), .Q(x1_q));  // open: clr
  and and_2 (and_2_out, decoder_1_out1, Write);
  Register #(.width(32)) x2 (.D(WData), .en(and_3_out), .clk(Clock_in), .Q(x2_q));  // open: clr
  and and_3 (and_3_out, decoder_1_out2, Write);
  Register #(.width(32)) x3 (.D(WData), .en(and_4_out), .clk(Clock_in), .Q(x3_q));  // open: clr
  and and_4 (and_4_out, decoder_1_out3, Write);
  Register #(.width(32)) x16 (.D(WData), .en(and_5_out), .clk(Clock_in), .Q(x16_q));  // open: clr
  and and_5 (and_5_out, decoder_1_out16, Write);
  Register #(.width(32)) register_1 (.D(WData), .en(and_6_out), .clk(Clock_in), .Q(register_1_q));  // open: clr
  and and_6 (and_6_out, decoder_1_out17, Write);
  Register #(.width(32)) register_2 (.D(WData), .en(and_7_out), .clk(Clock_in), .Q(register_2_q));  // open: clr
  and and_7 (and_7_out, decoder_1_out18, Write);
  Register #(.width(32)) register_3 (.D(WData), .en(and_8_out), .clk(Clock_in), .Q(register_3_q));  // open: clr
  and and_8 (and_8_out, decoder_1_out19, Write);
  and and_9 (and_9_out, decoder_1_out4, Write);
  and and_10 (and_10_out, decoder_1_out5, Write);
  and and_11 (and_11_out, decoder_1_out6, Write);
  and and_12 (and_12_out, decoder_1_out7, Write);
  and and_13 (and_13_out, decoder_1_out20, Write);
  and and_14 (and_14_out, decoder_1_out21, Write);
  and and_15 (and_15_out, decoder_1_out22, Write);
  and and_16 (and_16_out, decoder_1_out23, Write);
  Register #(.width(32)) x4 (.D(WData), .en(and_9_out), .clk(Clock_in), .Q(x4_q));  // open: clr
  Register #(.width(32)) x5 (.D(WData), .en(and_10_out), .clk(Clock_in), .Q(x5_q));  // open: clr
  Register #(.width(32)) x6 (.D(WData), .en(and_11_out), .clk(Clock_in), .Q(x6_q));  // open: clr
  Register #(.width(32)) x7 (.D(WData), .en(and_12_out), .clk(Clock_in), .Q(x7_q));  // open: clr
  Register #(.width(32)) register_4 (.D(WData), .en(and_13_out), .clk(Clock_in), .Q(register_4_q));  // open: clr
  Register #(.width(32)) x21 (.D(WData), .en(and_14_out), .clk(Clock_in), .Q(x21_q));  // open: clr
  Register #(.width(32)) register_5 (.D(WData), .en(and_15_out), .clk(Clock_in), .Q(register_5_q));  // open: clr
  Register #(.width(32)) register_6 (.D(WData), .en(and_16_out), .clk(Clock_in), .Q(register_6_q));  // open: clr
  Register #(.width(32)) x8 (.D(WData), .en(and_17_out), .clk(Clock_in), .Q(x8_q));  // open: clr
  and and_17 (and_17_out, decoder_1_out8, Write);
  Register #(.width(32)) x9 (.D(WData), .en(and_18_out), .clk(Clock_in), .Q(x9_q));  // open: clr
  and and_18 (and_18_out, decoder_1_out9, Write);
  Register #(.width(32)) x10 (.D(WData), .en(and_19_out), .clk(Clock_in), .Q(x10_q));  // open: clr
  and and_19 (and_19_out, decoder_1_out10, Write);
  Register #(.width(32)) x11 (.D(WData), .en(and_20_out), .clk(Clock_in), .Q(x11_q));  // open: clr
  and and_20 (and_20_out, decoder_1_out11, Write);
  Register #(.width(32)) register_7 (.D(WData), .en(and_21_out), .clk(Clock_in), .Q(register_7_q));  // open: clr
  and and_21 (and_21_out, decoder_1_out24, Write);
  Register #(.width(32)) register_8 (.D(WData), .en(and_22_out), .clk(Clock_in), .Q(register_8_q));  // open: clr
  and and_22 (and_22_out, decoder_1_out25, Write);
  Register #(.width(32)) x26 (.D(WData), .en(and_23_out), .clk(Clock_in), .Q(x26_q));  // open: clr
  and and_23 (and_23_out, decoder_1_out26, Write);
  Register #(.width(32)) register_9 (.D(WData), .en(and_24_out), .clk(Clock_in), .Q(register_9_q));  // open: clr
  and and_24 (and_24_out, decoder_1_out27, Write);
  and and_25 (and_25_out, decoder_1_out12, Write);
  and and_26 (and_26_out, decoder_1_out13, Write);
  and and_27 (and_27_out, decoder_1_out14, Write);
  and and_28 (and_28_out, decoder_1_out15, Write);
  and and_29 (and_29_out, decoder_1_out28, Write);
  and and_30 (and_30_out, decoder_1_out29, Write);
  and and_31 (and_31_out, decoder_1_out30, Write);
  and and_32 (and_32_out, decoder_1_out31, Write);
  Register #(.width(32)) x12 (.D(WData), .en(and_25_out), .clk(Clock_in), .Q(x12_q));  // open: clr
  Register #(.width(32)) x13 (.D(WData), .en(and_26_out), .clk(Clock_in), .Q(x13_q));  // open: clr
  Register #(.width(32)) x14 (.D(WData), .en(and_27_out), .clk(Clock_in), .Q(x14_q));  // open: clr
  Register #(.width(32)) x15 (.D(WData), .en(and_28_out), .clk(Clock_in), .Q(x15_q));  // open: clr
  Register #(.width(32)) register_10 (.D(WData), .en(and_29_out), .clk(Clock_in), .Q(register_10_q));  // open: clr
  Register #(.width(32)) register_11 (.D(WData), .en(and_30_out), .clk(Clock_in), .Q(register_11_q));  // open: clr
  Register #(.width(32)) register_12 (.D(WData), .en(and_31_out), .clk(Clock_in), .Q(register_12_q));  // open: clr
  Register #(.width(32)) x31 (.D(WData), .en(and_32_out), .clk(Clock_in), .Q(x31_q));  // open: clr
  Multiplexer #(.select(5), .width(32)) multiplexer_2 (
    .in0(x0_q), .in1(x1_q), .in2(x2_q), .in3(x3_q), .in4(x4_q), .in5(x5_q), .in6(x6_q), .in7(x7_q),
    .in8(x8_q), .in9(x9_q), .in10(x10_q), .in11(x11_q), .in12(x12_q), .in13(x13_q), .in14(x14_q),
    .in15(x15_q), .in16(x16_q), .in17(register_1_q), .in18(register_2_q), .in19(register_3_q),
    .in20(register_4_q), .in21(x21_q), .in22(register_5_q), .in23(register_6_q), .in24(register_7_q),
    .in25(register_8_q), .in26(x26_q), .in27(register_9_q), .in28(register_10_q), .in29(register_11_q),
    .in30(register_12_q), .in31(x31_q), .out(RData2), .sel(RReg2));
endmodule

module datapathControl (
);

  wire alu_ctrl_circuit_1_alu_src, and_1_out, branches_1_branch, clock_1_out, comparator_1_eq,
       comparator_1_gt, comparator_1_lt, main_control_circuit_1_branch, main_control_circuit_1_memread,
       main_control_circuit_1_memtoreg, main_control_circuit_1_memwrite, main_control_circuit_1_regwrite;
  wire [1:0] instruction_memory_1_instruction_2;
  wire [3:0] alu_ctrl_circuit_1_alu_ctrl0;
  wire [25:0] InstrReg_q;
  wire [31:0] adder_1_out, adder_2_out, data_memory_1_readdata, immgencircuit_1_imm32,
       instruction_memory_1_instruction, multiplexer_1_out, multiplexer_2_out, multiplexer_3_out,
       register32bit_1_rdata1, register32bit_1_rdata2, thirtytwobitalu_1_result;
  wire [31:26] InstrReg_q_2;

  Register #(.width(32)) InstrReg (
    .D(multiplexer_2_out), .en(1'b1), .clk(clock_1_out), .Q({InstrReg_q_2, InstrReg_q}));  // open: clr
  Adder #(.width(32)) adder_1 (.a({InstrReg_q_2, InstrReg_q}), .b(32'h4), .out(adder_1_out));  // open: cin, cout
  Clock clock_1 (.out(clock_1_out));
  instruction_memory instruction_memory_1 (
    .Address(InstrReg_q), .Clock(clock_1_out),
    .Instruction({instruction_memory_1_instruction[31:15], instruction_memory_1_instruction_2[1], instruction_memory_1_instruction[13], instruction_memory_1_instruction_2[0], instruction_memory_1_instruction[11:0]}));
  main_control_circuit main_control_circuit_1 (
    .I6_0(instruction_memory_1_instruction[6:0]), .MemtoReg(main_control_circuit_1_memtoreg),
    .RegWrite(main_control_circuit_1_regwrite), .MemRead(main_control_circuit_1_memread),
    .MemWrite(main_control_circuit_1_memwrite), .Branch(main_control_circuit_1_branch));
  Register32Bit register32bit_1 (
    .RReg1(instruction_memory_1_instruction[19:15]), .RReg2(instruction_memory_1_instruction[24:20]),
    .WReg(instruction_memory_1_instruction[11:7]), .WData(multiplexer_3_out),
    .Write(main_control_circuit_1_regwrite), .Clock_in(clock_1_out), .RData1(register32bit_1_rdata1),
    .RData2(register32bit_1_rdata2));
  ImmGenCircuit immgencircuit_1 (
    .Instr({instruction_memory_1_instruction[31:15], instruction_memory_1_instruction_2[1], instruction_memory_1_instruction[13], instruction_memory_1_instruction_2[0], instruction_memory_1_instruction[11:0]}),
    .Imm32(immgencircuit_1_imm32));
  ALU_Ctrl_Circuit alu_ctrl_circuit_1 (
    .I30(instruction_memory_1_instruction[30]), .I14(instruction_memory_1_instruction_2[1]),
    .I13(instruction_memory_1_instruction[13]), .I12(instruction_memory_1_instruction_2[0]),
    .I5(instruction_memory_1_instruction[5]), .I4(instruction_memory_1_instruction[4]),
    .ALU_Ctrl3(alu_ctrl_circuit_1_alu_ctrl0[3]), .ALU_Ctrl2(alu_ctrl_circuit_1_alu_ctrl0[2]),
    .ALU_Ctrl1(alu_ctrl_circuit_1_alu_ctrl0[1]), .ALU_Ctrl0(alu_ctrl_circuit_1_alu_ctrl0[0]),
    .ALU_Src(alu_ctrl_circuit_1_alu_src));
  Comparator #(.width(32)) comparator_1 (
    .a(register32bit_1_rdata1), .b(register32bit_1_rdata2), .gt(comparator_1_gt), .eq(comparator_1_eq),
    .lt(comparator_1_lt));
  Multiplexer #(.width(32)) multiplexer_1 (
    .in0(register32bit_1_rdata2), .in1(immgencircuit_1_imm32), .out(multiplexer_1_out),
    .sel(alu_ctrl_circuit_1_alu_src));
  Branches branches_1 (
    .bge(comparator_1_gt), .beq(comparator_1_eq), .blt(comparator_1_lt),
    .funct3(instruction_memory_1_instruction_2), .Branch(branches_1_branch));
  thirtyTwoBitALU thirtytwobitalu_1 (
    .CarryIn(1'b0), .ALU_Ctrl(alu_ctrl_circuit_1_alu_ctrl0), .A(register32bit_1_rdata1),
    .B(multiplexer_1_out), .Result(thirtytwobitalu_1_result));  // open: CarryOut
  and and_1 (and_1_out, main_control_circuit_1_branch, branches_1_branch);
  Adder #(.width(32)) adder_2 (
    .a({InstrReg_q_2, InstrReg_q}), .b(immgencircuit_1_imm32), .out(adder_2_out));  // open: cin, cout
  data_memory data_memory_1 (
    .Address(thirtytwobitalu_1_result[25:0]), .MemWrite(main_control_circuit_1_memwrite),
    .MemRead(main_control_circuit_1_memread), .ClockIn(clock_1_out), .WriteData(register32bit_1_rdata2),
    .ReadData(data_memory_1_readdata));
  Multiplexer #(.width(32)) multiplexer_2 (
    .in0(adder_1_out), .in1(adder_2_out), .out(multiplexer_2_out), .sel(and_1_out));
  Multiplexer #(.width(32)) multiplexer_3 (
    .in0(thirtytwobitalu_1_result), .in1(data_memory_1_readdata), .out(multiplexer_3_out),
    .sel(main_control_circuit_1_memtoreg));
endmodule

module ImmGenCircuit (
  input  [31:0] Instr,
  output [31:0] Imm32
);

  assign Imm32[31:12] = {{19{Instr[31]}}, Instr[31]};  // Bit_Extender bit_extender_1
  Multiplexer #(.select(2)) multiplexer_1 (
    .in0(Instr[20]), .in1(Instr[7]), .in2(1'b0), .out(Imm32[0]), .sel(Instr[6:5]));  // open: in3
  Multiplexer #(.width(4)) multiplexer_2 (.in0(Instr[24:21]), .in1(Instr[11:8]), .out(Imm32[4:1]), .sel(Instr[5]));
  Multiplexer multiplexer_3 (.in0(Instr[31]), .in1(Instr[7]), .out(Imm32[11]), .sel(Instr[6]));

  assign Imm32[10:5] = Instr[30:25];

  // Other names for the same wires on the sheet: I0 = Imm32[0]; I4_1[3:0] = Imm32[4:1]; I30_25[5:0] = Instr[30:25];
  //   I11 = Imm32[11]; I31_12[19:0] = Imm32[31:12]; I5 = Instr[5]; I6_5[1:0] = Instr[6:5]; I6 = Instr[6];
  //   I7 = Instr[7]; I11_8[3:0] = Instr[11:8]; I20 = Instr[20]; I24_21[3:0] = Instr[24:21]; I31 = Instr[31]
endmodule

module main_control_circuit (
  input  [6:0] I6_0,
  output MemtoReg,
  output RegWrite,
  output MemRead,
  output MemWrite,
  output Branch
);

  wire not_1_out, not_2_out;

  not not_1 (not_1_out, I6_0[6]);
  not not_2 (not_2_out, I6_0[5]);
  not not_3 (MemtoReg, I6_0[4]);
  or or_1 (RegWrite, not_2_out, I6_0[4]);
  and and_1 (MemRead, not_2_out, MemtoReg);
  and and_2 (MemWrite, not_1_out, I6_0[5], MemtoReg);

  assign Branch = I6_0[6];
endmodule

module instruction_memory (
  input  [25:0] Address,
  input  Clock,
  output [31:0] Instruction
);

  wire not_1_out;

  not not_1 (not_1_out, Clock);
  RAM #(.addrWidth(24), .dataWidth(32)) ram_1 (
    .addr(Address[25:2]), .we(1'b0), .oe(not_1_out), .clk(not_1_out), .dout(Instruction));  // open: din
endmodule

module data_memory (
  input  [25:0] Address,
  input  MemWrite,
  input  MemRead,
  input  ClockIn,
  input  [31:0] WriteData,
  output [31:0] ReadData
);

  wire [31:0] RAM0_dout, RAM1_dout, RAM2_dout, RAM3_dout;

  RAM #(.addrWidth(24), .asyncread("true"), .dataWidth(32)) RAM0 (
    .addr(Address[23:0]), .we(MemWrite), .oe(MemRead), .clk(ClockIn), .din(WriteData), .dout(RAM0_dout));
  RAM #(.addrWidth(24), .asyncread("true"), .dataWidth(32)) RAM1 (
    .addr(Address[23:0]), .we(MemWrite), .oe(MemRead), .clk(ClockIn), .din(WriteData), .dout(RAM1_dout));
  RAM #(.addrWidth(24), .dataWidth(32)) RAM2 (
    .addr(Address[23:0]), .we(MemWrite), .oe(MemRead), .clk(ClockIn), .din(WriteData), .dout(RAM2_dout));
  RAM #(.addrWidth(24), .dataWidth(32)) RAM3 (
    .addr(Address[23:0]), .we(MemWrite), .oe(MemRead), .clk(ClockIn), .din(WriteData), .dout(RAM3_dout));
  Multiplexer #(.select(2), .width(32)) multiplexer_1 (
    .in0(RAM0_dout), .in1(RAM1_dout), .in2(RAM2_dout), .in3(RAM3_dout), .out(ReadData), .sel(Address[25:24]));
endmodule

module Branches (
  input  bge,
  input  beq,
  input  blt,
  input  [1:0] funct3,
  output Branch
);

  wire not_1_out;

  not not_1 (not_1_out, beq);
  Multiplexer #(.select(2)) multiplexer_1 (
    .in0(beq), .in1(not_1_out), .in2(blt), .in3(bge), .out(Branch), .sel(funct3));
endmodule
